# Fritzing sketch lampwireless-d1 (saved by Fritzing 0.9.3b)
breadboards: 2

parts:
  WeMos_D1_Mini1 = WeMos D1 Mini
  RGB_Led = RGB LED - (4 legs) [package="5 mm [THT]"]
  LED = smd LED [color="Red (633nm)" package="0603 [SMD]"]
  VCC1 = Battery
  MOC3020 = MOC3031-M [package=dil06]
  216M = TRIAC [package=to-92]
  R1 = Resistor [tolerance=±5% resistance=47k package="1206 [SMD]"]
  220v_AC = Battery Holders [package=battcon_245mm]  # not connected
  S1 = Momentary Switch [package=ksa_sealed_tac_switch]
  LED_220v = Luxeon LED [package=luxeon]  # not connected

nets:
  N1: WeMos_D1_Mini1.3V3, RGB_Led.common_anode
  N2: WeMos_D1_Mini1.5V, VCC1.+
  N3: WeMos_D1_Mini1.D1, WeMos_D1_Mini1.G, LED.cathode, VCC1.-, MOC3020.1, MOC3020.2, S1.1, S1.2
  N4: WeMos_D1_Mini1.D2, RGB_Led.blue_cathode
  N5: WeMos_D1_Mini1.D3, S1.3, S1.4
  N6: WeMos_D1_Mini1.D5, RGB_Led.red_cathode
  N7: WeMos_D1_Mini1.D6, RGB_Led.green_cathode
  N8: WeMos_D1_Mini1.D7, LED.anode
  N9: MOC3020.4, MOC3020.6, 216M.M2, R1.Pin_0
